// Logisim project DedicatedStackMemory.circ as structural Verilog: 3 circuits, main circuit main
module \byte  (
  input  BitIn1,
  input  BitIn2,
  input  BitIn3,
  input  BitIn4,
  input  BitIn5,
  input  BitIn6,
  input  BitIn7,
  input  BitIn8,
  input  CLK,
  output BitOut1,
  output BitOut2,
  output BitOut3,
  output BitOut4,
  output BitOut5,
  output BitOut6,
  output BitOut7,
  output BitOut8
);

  D_Flip_Flop d_ff_1 (.D(BitIn1), .clk(CLK), .Q(BitOut1));  // open: Qn, preset, reset
  D_Flip_Flop d_ff_2 (.D(BitIn2), .clk(CLK), .Q(BitOut2));  // open: Qn, preset, reset
  D_Flip_Flop d_ff_3 (.D(BitIn3), .clk(CLK), .Q(BitOut3));  // open: Qn, preset, reset
  D_Flip_Flop d_ff_4 (.D(BitIn4), .clk(CLK), .Q(BitOut4));  // open: Qn, preset, reset
  D_Flip_Flop d_ff_5 (.D(BitIn5), .clk(CLK), .Q(BitOut5));  // open: Qn, preset, reset
  D_Flip_Flop d_ff_6 (.D(BitIn6), .clk(CLK), .Q(BitOut6));  // open: Qn, preset, reset
  D_Flip_Flop d_ff_7 (.D(BitIn7), .clk(CLK), .Q(BitOut7));  // open: Qn, preset, reset
  D_Flip_Flop d_ff_8 (.D(BitIn8), .clk(CLK), .Q(BitOut8));  // open: Qn, preset, reset
endmodule

module main (
  input  in_1,
  input  in_2,
  input  in_3,
  input  in_4,
  input  in_5,
  input  in_6,
  input  in_7,
  input  in_8,
  input  in_9,
  input  in_10,
  input  in_11
);

  wire and_1_out, and_2_out, and_3_out, and_4_out, dcr_1_sel1, dcr_1_sel2, dcr_1_sel3, dcr_1_sel4;

  dcr dcr_1 (
    .AddrBit2(in_10), .AddrBit1(in_11), .SEL1(dcr_1_sel1), .SEL2(dcr_1_sel2), .SEL3(dcr_1_sel3),
    .SEL4(dcr_1_sel4));
  and and_1 (and_1_out, dcr_1_sel1, in_9);
  and and_2 (and_2_out, dcr_1_sel2, in_9);
  and and_3 (and_3_out, dcr_1_sel3, in_9);
  and and_4 (and_4_out, dcr_1_sel4, in_9);
  \byte  byte_1 (
    .BitIn1(in_1), .BitIn2(in_2), .BitIn3(in_3), .BitIn4(in_4), .BitIn5(in_5), .BitIn6(in_6), .BitIn7(in_7),
    .BitIn8(in_8), .CLK(and_1_out));  // open: BitOut1, BitOut2, BitOut3, BitOut4, BitOut5, BitOut6, BitOut7, BitOut8
  \byte  byte_2 (
    .BitIn1(in_1), .BitIn2(in_2), .BitIn3(in_3), .BitIn4(in_4), .BitIn5(in_5), .BitIn6(in_6), .BitIn7(in_7),
    .BitIn8(in_8), .CLK(and_2_out));  // open: BitOut1, BitOut2, BitOut3, BitOut4, BitOut5, BitOut6, BitOut7, BitOut8
  \byte  byte_3 (
    .BitIn1(in_1), .BitIn2(in_2), .BitIn3(in_3), .BitIn4(in_4), .BitIn5(in_5), .BitIn6(in_6), .BitIn7(in_7),
    .BitIn8(in_8), .CLK(and_3_out));  // open: BitOut1, BitOut2, BitOut3, BitOut4, BitOut5, BitOut6, BitOut7, BitOut8
  \byte  byte_4 (
    .BitIn1(in_1), .BitIn2(in_2), .BitIn3(in_3), .BitIn4(in_4), .BitIn5(in_5), .BitIn6(in_6), .BitIn7(in_7),
    .BitIn8(in_8), .CLK(and_4_out));  // open: BitOut1, BitOut2, BitOut3, BitOut4, BitOut5, BitOut6, BitOut7, BitOut8
endmodule

module dcr (
  input  AddrBit2,
  input  AddrBit1,
  output SEL1,
  output SEL2,
  output SEL3,
  output SEL4
);

  wire not_1_out, not_2_out;

  not not_1 (not_1_out, AddrBit1);
  not not_2 (not_2_out, AddrBit2);
  nor nor_1 (SEL1, AddrBit2, AddrBit1);
  and and_1 (SEL2, AddrBit2, not_1_out);
  and and_2 (SEL3, not_2_out, AddrBit1);
  and and_3 (SEL4, AddrBit2, AddrBit1);
endmodule
