// Logisim project 8ByteStatic_RAM.circ as structural Verilog: 4 circuits, main circuit main
module \byte  (
  input  BitIn1,
  input  BitIn5,
  input  BitIn2,
  input  BitIn6,
  input  BitIn3,
  input  BitIn7,
  input  BitIn4,
  input  BitIn8,
  input  CLK,
  output BitOut1,
  output BitOut5,
  output BitOut2,
  output BitOut6,
  output BitOut3,
  output BitOut7,
  output BitOut4,
  output BitOut8
);

  D_Flip_Flop d_ff_1 (.D(BitIn1), .clk(CLK), .Q(BitOut1));  // open: Qn, preset, reset
  D_Flip_Flop d_ff_2 (.D(BitIn2), .clk(CLK), .Q(BitOut2));  // open: Qn, preset, reset
  D_Flip_Flop d_ff_3 (.D(BitIn3), .clk(CLK), .Q(BitOut3));  // open: Qn, preset, reset
  D_Flip_Flop d_ff_4 (.D(BitIn4), .clk(CLK), .Q(BitOut4));  // open: Qn, preset, reset
  D_Flip_Flop d_ff_5 (.D(BitIn5), .clk(CLK), .Q(BitOut5));  // open: Qn, preset, reset
  D_Flip_Flop d_ff_6 (.D(BitIn6), .clk(CLK), .Q(BitOut6));  // open: Qn, preset, reset
  D_Flip_Flop d_ff_7 (.D(BitIn7), .clk(CLK), .Q(BitOut7));  // open: Qn, preset, reset
  D_Flip_Flop d_ff_8 (.D(BitIn8), .clk(CLK), .Q(BitOut8));  // open: Qn, preset, reset
endmodule

module main (
  input  in_1,
  input  in_2
);

  wire byte_1_bitout1, byte_1_bitout2, byte_1_bitout3, byte_1_bitout4, byte_1_bitout5, byte_1_bitout6,
       byte_1_bitout7, byte_1_bitout8;

  LED led_1 (.in(byte_1_bitout1));
  \byte  byte_1 (
    .BitIn1(in_1), .BitIn5(in_1), .BitIn2(in_1), .BitIn6(in_1), .BitIn3(in_1), .BitIn7(in_1), .BitIn4(in_1),
    .BitIn8(in_1), .CLK(in_2), .BitOut1(byte_1_bitout1), .BitOut5(byte_1_bitout5), .BitOut2(byte_1_bitout2),
    .BitOut6(byte_1_bitout6), .BitOut3(byte_1_bitout3), .BitOut7(byte_1_bitout7), .BitOut4(byte_1_bitout4),
    .BitOut8(byte_1_bitout8));
  LED led_2 (.in(byte_1_bitout5));
  LED led_3 (.in(byte_1_bitout2));
  LED led_4 (.in(byte_1_bitout6));
  LED led_5 (.in(byte_1_bitout8));
  LED led_6 (.in(byte_1_bitout3));
  LED led_7 (.in(byte_1_bitout7));
  LED led_8 (.in(byte_1_bitout4));
endmodule

module SRAM (
  input  in_1,
  input  in_2,
  input  in_3,
  input  in_4,
  input  in_5,
  input  in_6,
  input  in_7,
  input  in_8,
  input  CLK,
  input  in_10,
  input  in_11,
  input  in_12
);

  wire and_1_out, and_2_out, and_3_out, and_4_out, and_5_out, and_6_out, and_7_out, and_8_out,
       byte_1_bitout1, byte_1_bitout2, byte_1_bitout3, byte_1_bitout4, byte_1_bitout5, byte_1_bitout6,
       byte_1_bitout7, byte_1_bitout8, dcr_1_sel1, dcr_1_sel2, dcr_1_sel3, dcr_1_sel4, dcr_1_sel5,
       dcr_1_sel6, dcr_1_sel7, dcr_1_sel8, dcr_2_sel1;

  dcr dcr_1 (
    .AddrBit3(in_10), .AddrBit2(in_11), .AddrBit1(in_12), .SEL1(dcr_1_sel1), .SEL2(dcr_1_sel2),
    .SEL3(dcr_1_sel3), .SEL4(dcr_1_sel4), .SEL5(dcr_1_sel5), .SEL6(dcr_1_sel6), .SEL7(dcr_1_sel7),
    .SEL8(dcr_1_sel8));
  and and_1 (and_1_out, dcr_1_sel1, CLK);
  and and_2 (and_2_out, dcr_1_sel2, CLK);
  and and_3 (and_3_out, dcr_1_sel3, CLK);
  and and_4 (and_4_out, dcr_1_sel4, CLK);
  \byte  byte_1 (
    .BitIn1(in_8), .BitIn5(in_4), .BitIn2(in_7), .BitIn6(in_3), .BitIn3(in_6), .BitIn7(in_2), .BitIn4(in_5),
    .BitIn8(in_1), .CLK(and_1_out), .BitOut1(byte_1_bitout1), .BitOut5(byte_1_bitout5),
    .BitOut2(byte_1_bitout2), .BitOut6(byte_1_bitout6), .BitOut3(byte_1_bitout3), .BitOut7(byte_1_bitout7),
    .BitOut4(byte_1_bitout4), .BitOut8(byte_1_bitout8));
  \byte  byte_2 (
    .BitIn1(in_8), .BitIn5(in_4), .BitIn2(in_7), .BitIn6(in_3), .BitIn3(in_6), .BitIn7(in_2), .BitIn4(in_5),
    .BitIn8(in_1), .CLK(and_2_out));  // open: BitOut1, BitOut5, BitOut2, BitOut6, BitOut3, BitOut7, BitOut4, BitOut8
  \byte  byte_3 (
    .BitIn1(in_8), .BitIn5(in_4), .BitIn2(in_7), .BitIn6(in_3), .BitIn3(in_6), .BitIn7(in_2), .BitIn4(in_5),
    .BitIn8(in_1), .CLK(and_3_out));  // open: BitOut1, BitOut5, BitOut2, BitOut6, BitOut3, BitOut7, BitOut4, BitOut8
  \byte  byte_4 (
    .BitIn1(in_8), .BitIn5(in_4), .BitIn2(in_7), .BitIn6(in_3), .BitIn3(in_6), .BitIn7(in_2), .BitIn4(in_5),
    .BitIn8(in_1), .CLK(and_4_out));  // open: BitOut1, BitOut5, BitOut2, BitOut6, BitOut3, BitOut7, BitOut4, BitOut8
  and and_5 (and_5_out, dcr_1_sel5, CLK);
  and and_6 (and_6_out, dcr_1_sel6, CLK);
  and and_7 (and_7_out, dcr_1_sel7, CLK);
  and and_8 (and_8_out, dcr_1_sel8, CLK);
  dcr dcr_2 (.SEL1(dcr_2_sel1));  // open: AddrBit3, AddrBit2, AddrBit1, SEL2, SEL3, SEL4, SEL5, SEL6, SEL7, SEL8
  \byte  byte_5 (
    .BitIn1(in_8), .BitIn5(in_4), .BitIn2(in_7), .BitIn6(in_3), .BitIn3(in_6), .BitIn7(in_2), .BitIn4(in_5),
    .BitIn8(in_1), .CLK(and_5_out));  // open: BitOut1, BitOut5, BitOut2, BitOut6, BitOut3, BitOut7, BitOut4, BitOut8
  \byte  byte_6 (
    .BitIn1(in_8), .BitIn5(in_4), .BitIn2(in_7), .BitIn6(in_3), .BitIn3(in_6), .BitIn7(in_2), .BitIn4(in_5),
    .BitIn8(in_1), .CLK(and_6_out));  // open: BitOut1, BitOut5, BitOut2, BitOut6, BitOut3, BitOut7, BitOut4, BitOut8
  \byte  byte_7 (
    .BitIn1(in_8), .BitIn5(in_4), .BitIn2(in_7), .BitIn6(in_3), .BitIn3(in_6), .BitIn7(in_2), .BitIn4(in_5),
    .BitIn8(in_1), .CLK(and_7_out));  // open: BitOut1, BitOut5, BitOut2, BitOut6, BitOut3, BitOut7, BitOut4, BitOut8
  \byte  byte_8 (
    .BitIn1(in_8), .BitIn5(in_4), .BitIn2(in_7), .BitIn6(in_3), .BitIn3(in_6), .BitIn7(in_2), .BitIn4(in_5),
    .BitIn8(in_1), .CLK(and_8_out));  // open: BitOut1, BitOut5, BitOut2, BitOut6, BitOut3, BitOut7, BitOut4, BitOut8
  // AND_Gate and_9 has open pins: in0=byte_1_bitout1, in1=dcr_2_sel1, out=open
  // AND_Gate and_10 has open pins: in0=byte_1_bitout2, in1=dcr_2_sel1, out=open
  // AND_Gate and_11 has open pins: in0=byte_1_bitout3, in1=dcr_2_sel1, out=open
  // AND_Gate and_12 has open pins: in0=byte_1_bitout4, in1=dcr_2_sel1, out=open
  // AND_Gate and_13 has open pins: in0=byte_1_bitout5, in1=dcr_2_sel1, out=open
  // AND_Gate and_14 has open pins: in0=byte_1_bitout6, in1=dcr_2_sel1, out=open
  // AND_Gate and_15 has open pins: in0=byte_1_bitout7, in1=dcr_2_sel1, out=open
  // AND_Gate and_16 has open pins: in0=byte_1_bitout8, in1=dcr_2_sel1, out=open
endmodule

module dcr (
  input  AddrBit3,
  input  AddrBit2,
  input  AddrBit1,
  output SEL1,
  output SEL2,
  output SEL3,
  output SEL4,
  output SEL5,
  output SEL6,
  output SEL7,
  output SEL8
);

  wire not_1_out, not_2_out, not_3_out, not_4_out, not_5_out, not_6_out, not_7_out, not_8_out, not_9_out;

  not not_1 (not_1_out, AddrBit2);
  and and_1 (SEL2, AddrBit3, not_1_out, not_2_out);
  not not_2 (not_2_out, AddrBit1);
  not not_3 (not_3_out, AddrBit3);
  and and_2 (SEL3, not_3_out, AddrBit2, not_4_out);
  not not_4 (not_4_out, AddrBit1);
  and and_3 (SEL4, AddrBit3, AddrBit2, not_5_out);
  not not_5 (not_5_out, AddrBit1);
  not not_6 (not_6_out, AddrBit3);
  not not_7 (not_7_out, AddrBit2);
  and and_4 (SEL5, not_6_out, not_7_out, AddrBit1);
  not not_8 (not_8_out, AddrBit2);
  and and_5 (SEL6, AddrBit3, not_8_out, AddrBit1);
  not not_9 (not_9_out, AddrBit3);
  and and_6 (SEL7, not_9_out, AddrBit2, AddrBit1);
  and and_7 (SEL8, AddrBit3, AddrBit2, AddrBit1);
  nor nor_1 (SEL1, AddrBit3, AddrBit2, AddrBit1);
endmodule
