// Logisim project ALUs_OPCODES.circ as structural Verilog: 2 circuits, main circuit LogicALU
module LogicALU (
  input  INP2,
  input  INP1,
  input  ADDRBIT2,
  input  ADDRBIT1,
  output OUT1
);

  wire and_1_out, nand_1_out, nor_1_out, xor_1_out;

  and and_1 (and_1_out, INP2, INP1);
  xor xor_1 (xor_1_out, INP2, INP1);
  nand nand_1 (nand_1_out, INP2, INP1);
  nor nor_1 (nor_1_out, INP2, INP1);
  MUX4_1 mux4_1_1 (
    .SIG4(nor_1_out), .SIG3(nand_1_out), .SIG2(xor_1_out), .SIG1(and_1_out), .ADDRBIT2(ADDRBIT2),
    .ADDRBIT1(ADDRBIT1), .OUT1(OUT1));
endmodule

module MUX4_1 (
  input  SIG4,
  input  SIG3,
  input  SIG2,
  input  SIG1,
  input  ADDRBIT2,
  input  ADDRBIT1,
  output OUT1
);

  wire and_1_out, and_2_out, and_3_out, and_4_out, and_5_out, and_6_out, and_7_out, and_8_out, not_1_out,
       not_2_out, not_3_out, not_4_out;

  not not_1 (not_1_out, ADDRBIT2);
  not not_2 (not_2_out, ADDRBIT1);
  not not_3 (not_3_out, ADDRBIT1);
  not not_4 (not_4_out, ADDRBIT2);
  and and_1 (and_1_out, not_1_out, not_2_out);
  and and_2 (and_2_out, ADDRBIT2, not_3_out);
  and and_3 (and_3_out, not_4_out, ADDRBIT1);
  and and_4 (and_4_out, ADDRBIT2, ADDRBIT1);
  and and_5 (and_5_out, SIG1, and_1_out);
  and and_6 (and_6_out, SIG2, and_2_out);
  and and_7 (and_7_out, SIG3, and_3_out);
  and and_8 (and_8_out, SIG4, and_4_out);
  or or_1 (OUT1, and_5_out, and_6_out, and_7_out, and_8_out);
endmodule
