// Logisim project DEMUXes.circ as structural Verilog
module router (
  input  InpAddr2,
  input  OutAddr2,
  input  InpAddr1,
  input  OutAddr1,
  input  Inp00,
  input  Inp01,
  input  Inp10,
  input  Inp11,
  output Out00,
  output Out01,
  output Out10,
  output Out11
);

  wire mux_1_selout;

  mux mux_1 (
    .Addr2(InpAddr2), .Addr1(InpAddr1), .Inp00(Inp00), .Inp01(Inp01), .Inp10(Inp10), .Inp11(Inp11),
    .SELOUT(mux_1_selout));
  demux demux_1 (
    .Addr2(OutAddr2), .Addr1(OutAddr1), .Inp(mux_1_selout), .Out1(Out00), .Out2(Out01), .Out3(Out10),
    .Out4(Out11));
endmodule

module demux (
  input  Addr2,
  input  Addr1,
  input  Inp,
  output Out1,
  output Out2,
  output Out3,
  output Out4
);

  wire and_1_out, and_2_out, and_3_out, nor_1_out, not_1_out, not_2_out;

  nor nor_1 (nor_1_out, Addr2, Addr1);
  and and_1 (and_1_out, Addr2, not_1_out);
  not not_1 (not_1_out, Addr1);
  not not_2 (not_2_out, Addr2);
  and and_2 (and_2_out, not_2_out, Addr1);
  and and_3 (and_3_out, Addr2, Addr1);
  and and_4 (Out1, Inp, nor_1_out);
  and and_5 (Out2, Inp, and_1_out);
  and and_6 (Out3, Inp, and_2_out);
  and and_7 (Out4, Inp, and_3_out);
endmodule

module mux (
  input  Addr2,
  input  Addr1,
  input  Inp00,
  input  Inp01,
  input  Inp10,
  input  Inp11,
  output SELOUT
);

  wire and_1_out, and_2_out, and_3_out, and_4_out, and_5_out, and_6_out, and_7_out, nor_1_out, not_1_out,
       not_2_out;

  nor nor_1 (nor_1_out, Addr2, Addr1);
  and and_1 (and_1_out, Addr2, not_1_out);
  not not_1 (not_1_out, Addr1);
  not not_2 (not_2_out, Addr2);
  and and_2 (and_2_out, not_2_out, Addr1);
  and and_3 (and_3_out, Addr2, Addr1);
  and and_4 (and_4_out, Inp00, nor_1_out);
  and and_5 (and_5_out, Inp01, and_1_out);
  and and_6 (and_6_out, Inp10, and_2_out);
  and and_7 (and_7_out, Inp11, and_3_out);
  or or_1 (SELOUT, and_4_out, and_5_out, and_6_out, and_7_out);
endmodule
