// Logisim project MUXes.circ as structural Verilog: 1 circuit, main circuit MUX4_1
module MUX4_1 (
  input  INP1,
  input  INP2,
  input  ADDRBIT2,
  input  INP3,
  input  ADDRBIT1,
  input  INP4,
  output DATA
);

  wire and_1_out, and_2_out, and_3_out, and_4_out, and_5_out, and_6_out, and_7_out, and_8_out, not_1_out,
       not_2_out, not_3_out, not_4_out;

  not not_1 (not_1_out, ADDRBIT2);
  not not_2 (not_2_out, ADDRBIT1);
  not not_3 (not_3_out, ADDRBIT1);
  not not_4 (not_4_out, ADDRBIT2);
  and and_1 (and_1_out, not_1_out, not_2_out);
  and and_2 (and_2_out, ADDRBIT2, not_3_out);
  and and_3 (and_3_out, not_4_out, ADDRBIT1);
  and and_4 (and_4_out, ADDRBIT2, ADDRBIT1);
  and and_5 (and_5_out, INP1, and_1_out);
  and and_6 (and_6_out, INP2, and_2_out);
  and and_7 (and_7_out, INP3, and_3_out);
  and and_8 (and_8_out, INP4, and_4_out);
  or or_1 (DATA, and_5_out, and_6_out, and_7_out, and_8_out);
endmodule
