// Logisim project MultiLUT.circ as structural Verilog
module LUT2_1 (
  input  ADDR1,
  input  ADDR2,
  input  WE,
  input  CLK,
  input  DATA
);

  wire and_1_out, and_2_out, and_3_out, and_4_out, and_5_out, and_6_out, and_7_out, nor_1_out, not_1_out,
       not_2_out;

  not not_1 (not_1_out, ADDR2);
  not not_2 (not_2_out, ADDR2);
  nor nor_1 (nor_1_out, ADDR1, ADDR2);
  and and_1 (and_1_out, ADDR1, not_1_out);
  and and_2 (and_2_out, not_2_out, ADDR2);
  and and_3 (and_3_out, not_2_out, ADDR2);
  and and_4 (and_4_out, nor_1_out, WE, CLK);
  and and_5 (and_5_out, and_1_out, WE, CLK);
  and and_6 (and_6_out, and_2_out, WE, CLK);
  and and_7 (and_7_out, and_3_out, WE, CLK);
  D_Flip_Flop d_ff_1 (.D(DATA), .clk(and_4_out));  // open: Q, Qn, preset, reset
  D_Flip_Flop d_ff_2 (.D(DATA), .clk(and_5_out));  // open: Q, Qn, preset, reset
  D_Flip_Flop d_ff_3 (.D(DATA), .clk(and_6_out));  // open: Q, Qn, preset, reset
  D_Flip_Flop d_ff_4 (.D(DATA), .clk(and_7_out));  // open: Q, Qn, preset, reset
endmodule
