// Logisim project crossBarSwitches.circ as structural Verilog: 2 circuits, main circuit main
module crossbarSwitch (
  input  enable1_1,
  input  enable1_2,
  input  enable1_3,
  input  inputbit1,
  input  inputbit2,
  input  inputbit3,
  input  enable2_1,
  input  enable2_2,
  input  enable2_3,
  input  enable3_1,
  input  enable3_2,
  input  enable3_3,
  output out1,
  output out2,
  output out3
);

  and and_1 (out1, inputbit3, enable1_3);
  and and_2 (out2, inputbit3, enable2_3);
  and and_3 (out3, inputbit3, enable3_3);
  and and_4 (out1, inputbit2, enable1_2);
  and and_5 (out2, inputbit2, enable2_2);
  and and_6 (out3, inputbit2, enable3_2);
  and and_7 (out1, inputbit1, enable1_1);
  and and_8 (out2, inputbit1, enable2_1);
  and and_9 (out3, inputbit1, enable3_1);

  // Notes on the sheet:
  //   and_1 drives only 1 and floats otherwise
  //   and_2 drives only 1 and floats otherwise
  //   and_3 drives only 1 and floats otherwise
  //   and_4 drives only 1 and floats otherwise
  //   and_5 drives only 1 and floats otherwise
  //   and_6 drives only 1 and floats otherwise
  //   and_7 drives only 1 and floats otherwise
  //   and_8 drives only 1 and floats otherwise
  //   and_9 drives only 1 and floats otherwise
endmodule

module main (
  input  in_1,
  input  in_2,
  input  in_3,
  input  in_4,
  input  in_5,
  input  in_6,
  input  in_7,
  input  in_8,
  input  in_9,
  input  in_10,
  input  in_11,
  input  in_12,
  output out_13,
  output out_14,
  output out_15
);

  crossbarSwitch crossbarswitch_1 (
    .enable1_1(in_1), .enable1_2(in_2), .enable1_3(in_3), .inputbit1(in_4), .inputbit2(in_5),
    .inputbit3(in_6), .enable2_1(in_7), .enable2_2(in_8), .enable2_3(in_9), .enable3_1(in_10),
    .enable3_2(in_11), .enable3_3(in_12), .out1(out_13), .out2(out_14), .out3(out_15));
endmodule
