// Logisim project logevol2.circ as structural Verilog: 1 circuit, main circuit main
module main (
  input  in_1,
  input  in_2,
  input  in_3,
  input  in_4,
  input  in_5,
  input  in_6,
  input  in_7,
  input  in_8,
  input  in_9
);

  wire n74670_1_pin6, n74670_1_pin7, n74670_1_pin9, n74670_1_pin10, n74670_1_pin11, n74670_1_pin12;

  _74670 #(.ShowInternalStructure("true")) u_74670_1 (
    .pin1(in_7), .pin2(in_8), .pin3(in_9), .pin4(in_5), .pin5(in_4), .pin6(n74670_1_pin6),
    .pin7(n74670_1_pin7), .pin15(in_6), .pin14(in_3), .pin13(in_2), .pin12(n74670_1_pin12),
    .pin11(n74670_1_pin11), .pin10(n74670_1_pin10), .pin9(n74670_1_pin9));
  not not_1 (n74670_1_pin12, in_1);
  LedBar #(.matrixcols(4)) ledbar_1 (
    .led0(n74670_1_pin10), .led1(n74670_1_pin9), .led2(n74670_1_pin7), .led3(n74670_1_pin6));
  // also tied to GND on the sheet: n74670_1_pin11
endmodule
