// Logisim project logevol3.circ as structural Verilog: 4 circuits, main circuit main
module main (
  input  DIN1,
  input  DIN2,
  input  DIN3,
  input  DIN4,
  input  OADDR1,
  input  OADDR2,
  input  IADDR1,
  input  IADDR2,
  output OUT1,
  output OUT2,
  output OUT3,
  output OUT4
);

  FFR ffr_1 (
    .DIN1(DIN1), .DIN2(DIN2), .OUTADDRBIT1(OADDR1), .DIN3(DIN3), .OUTADDRBIT2(OADDR2), .DIN4(DIN4),
    .INPADDRBIT1(IADDR1), .INPADDRBIT2(IADDR2), .DOUT1(OUT1), .DOUT2(OUT2), .DOUT3(OUT3), .DOUT4(OUT4));
endmodule

module FFMUX (
  input  DIN1,
  input  DIN2,
  input  DIN3,
  input  DIN4,
  input  ADDRBIT1,
  input  ADDRBIT2,
  output DOUT
);

  wire and_1_out, and_2_out, and_3_out, and_4_out, and_5_out, and_6_out, and_7_out, nor_1_out, not_1_out,
       not_2_out;

  not not_1 (not_1_out, ADDRBIT1);
  not not_2 (not_2_out, ADDRBIT2);
  nor nor_1 (nor_1_out, ADDRBIT1, ADDRBIT2);
  and and_1 (and_1_out, not_1_out, ADDRBIT2);
  and and_2 (and_2_out, ADDRBIT1, not_2_out);
  and and_3 (and_3_out, ADDRBIT1, ADDRBIT2);
  and and_4 (and_4_out, DIN1, nor_1_out);
  and and_5 (and_5_out, DIN2, and_1_out);
  and and_6 (and_6_out, DIN3, and_2_out);
  and and_7 (and_7_out, DIN4, and_3_out);
  or or_1 (DOUT, and_4_out, and_5_out, and_6_out, and_7_out);
endmodule

module FFDEMUX (
  input  DIN,
  input  ADDRBIT1,
  input  ADDRBIT2,
  output DOUT1,
  output DOUT2,
  output DOUT3,
  output DOUT4
);

  wire and_1_out, and_2_out, and_3_out, nor_1_out, not_1_out, not_2_out;

  not not_1 (not_1_out, ADDRBIT1);
  not not_2 (not_2_out, ADDRBIT2);
  nor nor_1 (nor_1_out, ADDRBIT1, ADDRBIT2);
  and and_1 (and_1_out, not_1_out, ADDRBIT2);
  and and_2 (and_2_out, ADDRBIT1, not_2_out);
  and and_3 (and_3_out, ADDRBIT1, ADDRBIT2);
  and and_4 (DOUT1, DIN, nor_1_out);
  and and_5 (DOUT2, DIN, and_1_out);
  and and_6 (DOUT3, DIN, and_2_out);
  and and_7 (DOUT4, DIN, and_3_out);
endmodule

module FFR (
  input  DIN1,
  input  DIN2,
  input  OUTADDRBIT1,
  input  DIN3,
  input  OUTADDRBIT2,
  input  DIN4,
  input  INPADDRBIT1,
  input  INPADDRBIT2,
  output DOUT1,
  output DOUT2,
  output DOUT3,
  output DOUT4
);

  wire ffmux_1_dout;

  FFMUX ffmux_1 (
    .DIN1(DIN1), .DIN2(DIN2), .DIN3(DIN3), .DIN4(DIN4), .ADDRBIT1(INPADDRBIT1), .ADDRBIT2(INPADDRBIT2),
    .DOUT(ffmux_1_dout));
  FFDEMUX ffdemux_1 (
    .DIN(ffmux_1_dout), .ADDRBIT1(OUTADDRBIT1), .ADDRBIT2(OUTADDRBIT2), .DOUT1(DOUT1), .DOUT2(DOUT2),
    .DOUT3(DOUT3), .DOUT4(DOUT4));
endmodule
